# Fritzing sketch Platine_02v1 (saved by Fritzing 0.9.4)
breadboards: 1

parts:
  IC1 = IC, DIP package, 14 pins [chip_label=IC]
  IC2 = IC, DIP package, 14 pins [chip_label=IC]
  IC3 = IC, DIP package, 14 pins [chip_label=IC]
  IC4 = IC, DIP package, 14 pins [chip_label=IC]  # not connected
  Supply_5V = female pin header, 2 pins [form="♀ (female)"]
  JST_Connector_0 = female pin header, 10 pins [form="♀ (female)"]
  R1 = Resistor [tolerance=±5% resistance=3.3 package=THT]
  R2 = Resistor [tolerance=±5% resistance=3.3 package=THT]
  R3 = Resistor [tolerance=±5% resistance=3.3 package=THT]
  R4 = Resistor [tolerance=±5% resistance=3.3 package=THT]
  R5 = Resistor [tolerance=±5% resistance=3.3 package=THT]
  R6 = Resistor [tolerance=±5% resistance=3.3 package=THT]
  U1 = 74HC595 [package="DIP16 [THT]"]
  D1 = Diode [package=diode-1n4148]
  C2 = Electrolytic Capacitor [capacitance=10µF package="100 mil [THT, electrolytic]"]
  L1 = Solenoid
  D2 = Diode [package=diode-1n4148]
  C3 = Electrolytic Capacitor [capacitance=10µF package="100 mil [THT, electrolytic]"]
  L2 = Solenoid
  D3 = Diode [package=diode-1n4148]
  C4 = Electrolytic Capacitor [capacitance=10µF package="100 mil [THT, electrolytic]"]
  L3 = Solenoid
  D4 = Diode [package=diode-1n4148]
  C5 = Electrolytic Capacitor [capacitance=10µF package="100 mil [THT, electrolytic]"]
  L4 = Solenoid
  D5 = Diode [package=diode-1n4148]
  C6 = Electrolytic Capacitor [capacitance=10µF package="100 mil [THT, electrolytic]"]
  L5 = Solenoid
  D6 = Diode [package=diode-1n4148]
  C7 = Electrolytic Capacitor [capacitance=10µF package="100 mil [THT, electrolytic]"]
  L6 = Solenoid
  Supply_12V = female pin header, 2 pins [form="♀ (female)"]
  Q6 = NPN-Transistor [package="TO92 [THT]"]
  Q5 = NPN-Transistor [package="TO92 [THT]"]
  Q4 = NPN-Transistor [package="TO92 [THT]"]
  Q3 = NPN-Transistor [package="TO92 [THT]"]
  Q2 = NPN-Transistor [package="TO92 [THT]"]
  Q1 = NPN-Transistor [package="TO92 [THT]"]

nets:
  N1: IC1.pin1, IC1.pin4, IC1.pin10, IC1.pin13, IC2.pin1, IC2.pin4, IC2.pin10, IC2.pin13, JST_Connector_0.pin1
  N2: IC1.pin2, JST_Connector_0.pin4
  N3: IC1.pin3, R3.Pin_0
  N4: IC1.pin5, JST_Connector_0.pin5
  N5: IC1.pin6, R4.Pin_0
  N6: IC1.pin8, IC1.pin9, JST_Connector_0.pin9
  N7: IC1.pin11, IC1.pin12, JST_Connector_0.pin8
  N8: IC1.pin14, IC2.pin14, IC3.pin14, Supply_5V.pin1, U1.VCC
  N9: IC2.pin2, JST_Connector_0.pin2
  N10: IC2.pin3, R1.Pin_0
  N11: IC2.pin5, JST_Connector_0.pin3
  N12: IC2.pin6, R2.Pin_0
  N13: IC2.pin7, IC3.pin7, Supply_5V.pin2, U1.GND, C2.-, C3.-, C4.-, C5.-, C6.-, C7.-, Supply_12V.pin2, Q6.E, Q5.E, Q4.E, Q3.E, Q2.E, Q1.E
  N14: IC2.pin8, R6.Pin_0
  N15: IC2.pin9, JST_Connector_0.pin7
  N16: IC2.pin11, R5.Pin_0
  N17: IC2.pin12, JST_Connector_0.pin6
  N18: R1.Pin_1, Q1.B
  N19: R2.Pin_1, Q2.B
  N20: R3.Pin_1, Q3.B
  N21: R4.Pin_1, Q4.B
  N22: R5.Pin_1, Q5.B
  N23: R6.Pin_1, Q6.B
  N24: D1.A, C2.+, L1.pin2, Q1.C
  N25: D1.C, L1.pin1, D2.C, L2.pin1, D3.C, L3.pin1, D4.C, L4.pin1, D5.C, L5.pin1, D6.C, L6.pin1, Supply_12V.pin1
  N26: D2.A, C3.+, L2.pin2, Q2.C
  N27: D3.A, C4.+, L3.pin2, Q3.C
  N28: D4.A, C5.+, L4.pin2, Q4.C
  N29: D5.A, C6.+, L5.pin2, Q5.C
  N30: D6.A, C7.+, L6.pin2, Q6.C

notes:
  PWM
  Sig 0-7
  Uebertrag
